# Fritzing sketch Camera_Remote (saved by Fritzing 0.9.3b)
stripboards: 1

parts:
  WeMos_D1_Mini1 = WeMos D1 Mini
  BAT1 = LIPO-2000mAh [package=lipo-2000]
  S1 = Toggle Switch [package=THT]
  U1 = Sharp PC817 [package=THT]
  R1 = Resistor [tolerance=±5% resistance=220 package=THT]
  S2 = Round Pushbutton
  TRS1 = Audio Jack (TRS) 3.5mm [package="4Ucon 08780 [THT]"]
  R2 = Resistor [tolerance=±5% resistance=220 package=THT]

nets:
  N1: WeMos_D1_Mini1.5V, S1.L2
  N2: WeMos_D1_Mini1.D1, R1.Pin_0, S2.leg0
  N3: WeMos_D1_Mini1.G, BAT1.-, U1.Pin_2
  N4: BAT1.+, S1.COM
  N5: S1.L1, S2.leg1
  N6: U1.Pin_1, R1.Pin_1
  N7: U1.Pin_4, TRS1.Tip
  N8: U1.Pin_3, R2.Pin_0
  N9: TRS1.Sleeve, R2.Pin_1
